# Fritzing sketch CyLights (saved by Fritzing 0.9.3b)
circuit board: 17.211cm x 8.88956cm
breadboards: 3

parts:
  MCP23016 = MCP23016 [package="DIP (Dual Inline) [THT]"]
  J2 = Screw terminal - 2 pins [package=THT]
  Adafruit_Huzzah_ESP8266 = Adafruit HUZZAH ESP8266 [part_number="Adafruit #2471"]
  U1 = AQW214 [package="DIP (Dual Inline) [THT]"]
  U2 = AQW214 [package="DIP (Dual Inline) [THT]"]
  U3 = AQW214 [package="DIP (Dual Inline) [THT]"]
  U4 = AQW214 [package="DIP (Dual Inline) [THT]"]
  U5 = AQW214 [package="DIP (Dual Inline) [THT]"]
  U6 = DIP - 14 pins [package="DIP (Dual Inline) [THT]"]
  J3 = Screw terminal - 2 pins [package=THT]
  J4 = Screw terminal - 2 pins [package=THT]
  J5 = Screw terminal - 2 pins [package=THT]
  J6 = Screw terminal - 2 pins [package=THT]
  J7 = Screw terminal - 2 pins [package=THT]
  R1 = Resistor [tolerance=±5% resistance=3.3k package=THT]
  C1 = Ceramic Capacitor [capacitance=1pF package="100 mil [THT, multilayer]"]
  C2 = Ceramic Capacitor [capacitance=0.1mF package="100 mil [THT, multilayer]"]
  LED1 = LED - 5mm [color="Green (570nm)" package="5 mm [THT]"]
  R2 = Resistor [tolerance=±5% resistance=150 package=THT]
  J1 = Screw terminal - 2 pins [package=THT]
  LED2 = LED - 5mm [color="Red (633nm)" package="5 mm [THT]"]
  LED3 = LED - 5mm [color="Red (633nm)" package="5 mm [THT]"]
  LED4 = LED - 5mm [color="Red (633nm)" package="5 mm [THT]"]
  LED5 = LED - 5mm [color="Red (633nm)" package="5 mm [THT]"]
  LED6 = LED - 5mm [color="Red (633nm)" package="5 mm [THT]"]
  R3 = Resistor [tolerance=±5% resistance=150 package=THT]
  R4 = Resistor [tolerance=±5% resistance=150 package=THT]
  R5 = Resistor [tolerance=±5% resistance=150 package=THT]
  R6 = Resistor [tolerance=±5% resistance=150 package=THT]
  R7 = Resistor [tolerance=±5% resistance=150 package=THT]
  C3 = Electrolytic Capacitor [capacitance=0.22mF package="100 mil [THT, electrolytic]"]
  C4 = Ceramic Capacitor [capacitance=0.47mF package="100 mil [THT, multilayer]"]
  C5 = Tantalum Capacitor [capacitance=1μF package="100 mil [THT, tantalum]"]
  LED7 = LED - 5mm [color="Yellow (595nm)" package="5 mm [THT]"]
  IC1 = Voltage Regulator [package=to-220-alt]
  IC2 = Voltage Regulator [package=78xxl]

nets:
  N1: MCP23016.GP1.0, U1.R2_-_VCC
  N2: MCP23016.GP1.1, U2.R1_-_VCC
  N3: MCP23016.GP1.2, U2.R2_-_VCC
  N4: MCP23016.GP1.3, U3.R1_-_VCC
  N5: MCP23016.GP1.4, U4.R1_-_VCC
  N6: MCP23016.CLK, R1.Pin_0, C1.0
  N7: MCP23016.GP1.5, U1.R1_-_VCC
  N8: MCP23016.GP1.6, U4.R2_-_VCC
  N9: MCP23016.GP1.7, U3.R2_-_VCC
  N10: MCP23016.SCL, Adafruit_Huzzah_ESP8266.GPIO4
  N11: MCP23016.SDA, Adafruit_Huzzah_ESP8266.GPIO5
  N12: MCP23016.A0, MCP23016.A1, MCP23016.A2, MCP23016.VSS#18, U6.COM, C1.1
  N13: MCP23016.GP0.0, U5.R1_-_VCC
  N14: MCP23016.GP0.1, U5.R2_-_VCC
  N15: MCP23016.GP0.2, LED2.anode
  N16: MCP23016.GP0.3, LED3.anode
  N17: MCP23016.GP0.4, LED4.anode
  N18: MCP23016.GP0.5, LED5.anode
  N19: MCP23016.GP0.6, LED6.anode
  GND: J2.pin1, Adafruit_Huzzah_ESP8266.GND, C2.0, R2.Pin_0, J1.pin2, R3.Pin_0, R4.Pin_0, R5.Pin_0, R6.Pin_0, R7.Pin_0, C3.+, C4.1, C5.-, LED7.cathode, IC1.IN, IC2.GND
  N20: J2.pin2, U1.R2_-_COM, U1.R1_-_COM, U2.R2_-_COM, U2.R1_-_COM, U3.R2_-_COM, U3.R1_-_COM, U4.R2_-_COM, U4.R1_-_COM, U5.R2_-_COM, U5.R1_-_COM, J1.pin1, C4.0, IC1.GND
  N21: Adafruit_Huzzah_ESP8266.VIN, R1.Pin_1, C2.1, LED1.anode, IC2.OUT
  N22: Adafruit_Huzzah_ESP8266.GPIO14, LED7.anode
  N23: U1.R1_-_GND, U6.R1
  N24: U1.R2_-_GND, U6.R2
  N25: U1.R2_-_NO, J3.pin2
  N26: U1.R1_-_NO, J3.pin1
  N27: U2.R1_-_GND, U6.R3
  N28: U2.R2_-_GND, U6.R4
  N29: U2.R2_-_NO, J4.pin2
  N30: U2.R1_-_NO, J4.pin1
  N31: U3.R1_-_GND, U6.R5
  N32: U3.R2_-_GND, U6.R6
  N33: U3.R2_-_NO, J5.pin2
  N34: U3.R1_-_NO, J5.pin1
  N35: U4.R1_-_GND, U6.R7
  N36: U4.R2_-_GND, U6.R8
  N37: U4.R2_-_NO, J6.pin2
  N38: U4.R1_-_NO, J6.pin1
  N39: U5.R1_-_GND, U6.R9
  N40: U5.R2_-_GND, U6.R10
  N41: U5.R2_-_NO, J7.pin2
  N42: U5.R1_-_NO, J7.pin1
  N43: LED1.cathode, R2.Pin_1
  N44: LED2.cathode, R3.Pin_1
  N45: LED3.cathode, R4.Pin_1
  N46: LED4.cathode, R5.Pin_1
  N47: LED5.cathode, R6.Pin_1
  N48: LED6.cathode, R7.Pin_1
  N49: C3.-, C5.+, IC1.OUT, IC2.IN

notes:
  12VDC IN
  12VDC OUT
  Act
  PWR
  CyLights, CyLights IoT Control Board, 1.0
  12VDC Out
  L1 On/L1 Off
  L2 On/L2 Off
  L3 On/L3 Off
  L4 On/L4 Off
  L5 On/L5 Off
  12VDC In
  CyLights Board Rev 1.0
  -
  +

custom parts:
  MCP23016: An I2C BUS 16 bit I/O expander.
  Adafruit HUZZAH ESP8266: Add Internet to your next project with an adorable, bite-sized WiFi microcontroller, at a price you like! The ESP8266 processor from Espressif is an 80 MHz microcontroller with a full WiFi front-end (both as client and access point) and TCP/IP stack with DNS support as well. While this chip has been very popular, its also been very difficult to use. Most of the low cost modules are not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
  AQW214: Panasonic PhotoMOS Compact DIP8-pin type of 60V to 600V load voltage
  DIP - 14 pins: Bourns 4114-R-151 bussed 150 Ohm resistor pack IC
  Voltage Regulator: Voltage Regulator Standard LM2940CT 9V regulator. IGO (Input Ground Output).
